# Fritzing sketch LineFollower2sensor (saved by Fritzing 0.9.3b)
breadboards: 1

parts:
  M1 = fc-51 [package=THT]
  M2 = fc-51 [package=THT]
  Part1 = Arduino Uno (Rev3)
  IC1 = L293D [package=THT]
  M3 = DC Motor
  M4 = DC Motor

nets:
  N1: M1.pin1, Part1.D2
  N2: M1.pin2, M2.pin2, IC1.0V
  N3: M1.pin3, M2.pin3, IC1.Enable_1, IC1.+Vmotor, IC1.Enable_2, IC1.+V
  N4: M2.pin1, Part1.D3_PWM
  N5: Part1.D4, IC1.In_1
  N6: Part1.D5_PWM, IC1.In_2
  N7: Part1.D6_PWM, IC1.In_3
  N8: Part1.D7, IC1.In_4
  N9: IC1.Out_1_(_Controlled_by_Enable_1_), M4.pin_1
  N10: IC1.Out_2_(_Controlled_by_Enable_1_), M4.pin_2
  N11: IC1.Out_3_(_Controlled_by_Enable_2_), M3.pin_2
  N12: IC1.Out_4_(_Controlled_by_Enable_2_), M3.pin_1
